# Fritzing sketch NanoSketch1.0 (saved by Fritzing 0.9.3b)
breadboards: 1

parts:
  J1 = Basic Servo
  Part1 = Arduino Nano (Rev3.0)
  HC-SR04_Sensor_1 = HC-SR04 Ultrasonic Distance Sensor
  Part2 = Arduino Nano (Rev3.0)
  HC-SR04_Sensor_2 = HC-SR04 Ultrasonic Distance Sensor
  JACK1 = 2.1mm Barrel Jack with Terminal Block
  VALVE1 = Plastic Solenoid Valve
  Part3 = KY-019 5V Relay Module [package="Breakout board"]
  D1 = Diode [package=diode-1n4148]
  IC1 = Voltage Regulator [package=to-220-alt]
  C2 = Electrolytic Capacitor [capacitance=0.1µF package="0807 [SMD, electrolytic]"]
  C3 = Electrolytic Capacitor [capacitance=0.1µF package="0807 [SMD, electrolytic]"]

nets:
  GND: J1.gnd, Part1.GND, HC-SR04_Sensor_1.GND, Part2.GND, HC-SR04_Sensor_2.GND, JACK1.NEG, VALVE1.no_name_yet#2, Part3.-, D1.C, IC1.IN, C2.-, C3.-
  VCC: J1.vcc, Part1.5V, HC-SR04_Sensor_1.VCC, Part2.5V, HC-SR04_Sensor_2.VCC, Part3.+
  N1: J1.pulse, Part1.D3
  N2: Part1.D4, HC-SR04_Sensor_1.ECHO
  N3: Part1.D5, HC-SR04_Sensor_1.TRIG
  N4: Part2.D2, Part3.S
  N5: Part2.D4, HC-SR04_Sensor_2.ECHO
  N6: Part2.D5, HC-SR04_Sensor_2.TRIG
  VIN: Part2.VIN, IC1.GND, C2.+
  N7: JACK1.POS, Part3.Common, IC1.OUT, C3.+
  N8: VALVE1.no_name_yet#1, Part3.NO, D1.A

custom parts:
  KY-019 5V Relay Module: KY-019 5V Relay module, used to control AC circuits.
