# Fritzing sketch UnoSketch (saved by Fritzing 0.9.3b)
breadboards: 1

parts:
  JACK2 = 2.1mm Barrel Jack with Terminal Block
  VALVE2 = Plastic Solenoid Valve
  Part4 = KY-019 5V Relay Module [package="Breakout board"]
  D2 = Diode [package=diode-1n4148]
  IC2 = Voltage Regulator [package=to-220-alt]
  C4 = Electrolytic Capacitor [capacitance=0.1µF package="0807 [SMD, electrolytic]"]
  C5 = Electrolytic Capacitor [capacitance=0.1µF package="0807 [SMD, electrolytic]"]
  Part5 = Arduino Uno (Rev3)
  hc-sr3 = hc-sr04
  hc-sr4 = hc-sr04
  J1 = Basic Servo

nets:
  N1: JACK2.POS, Part4.Common, C5.+
  N2: JACK2.NEG, VALVE2.no_name_yet#2, D2.C, C5.-
  N3: VALVE2.no_name_yet#1, Part4.NO, D2.A
  N4: Part4.S, Part5.D5_PWM
  VCC: Part4.+, Part5.5V, hc-sr3.VCC, hc-sr4.VCC, J1.vcc
  GND: Part4.-, Part5.GND, hc-sr3.GND, hc-sr4.GND, J1.gnd
  GND_2: IC2.GND, C4.+, Part5.VIN
  N5: Part5.D9_PWM, J1.pulse
  N6: Part5.D10_PWM/SS, hc-sr3.Echo
  N7: Part5.D11_PWM/MOSI, hc-sr3.Trig
  N8: Part5.D2, hc-sr4.Trig
  N9: Part5.D3_PWM, hc-sr4.Echo

custom parts:
  KY-019 5V Relay Module: KY-019 5V Relay module, used to control AC circuits.
